# Fritzing sketch stoply (saved by Fritzing 1.0.2b)
breadboards: 4

parts:
  Part1 = Arduino Uno (Rev3)
  LED4 = LED - 5mm [color="Green (555nm)" current=0.030A package="5 mm [THT]"]
  LED5 = LED - 5mm [color="Yellow (585nm)" current=0.030A package="5 mm [THT]"]
  LED6 = LED - 5mm [color="Red (633nm)" current=0.030A package="5 mm [THT]"]
  R2 = Resistor [tolerance=±5% power=0.25W resistance=220 package=THT]
  LED7 = LED - 5mm [color="Red (633nm)" current=0.030A package="5 mm [THT]"]
  R3 = Resistor [tolerance=±5% power=0.25W resistance=220 package=THT]
  LED8 = LED - 5mm [color="Yellow (585nm)" current=0.030A package="5 mm [THT]"]
  LED9 = LED - 5mm [color="Green (555nm)" current=0.030A package="5 mm [THT]"]
  LED10 = LED - 5mm [color="Green (555nm)" current=0.030A package="5 mm [THT]"]
  LED11 = LED - 5mm [color="Yellow (585nm)" current=0.030A package="5 mm [THT]"]
  LED12 = LED - 5mm [color="Red (633nm)" current=0.030A package="5 mm [THT]"]
  R4 = Resistor [tolerance=±5% power=0.25W resistance=220 package=THT]
  LED13 = LED - 5mm [color="Green (555nm)" current=0.030A package="5 mm [THT]"]
  LED14 = LED - 5mm [color="Yellow (585nm)" current=0.030A package="5 mm [THT]"]
  LED15 = LED - 5mm [color="Red (633nm)" current=0.030A package="5 mm [THT]"]
  R5 = Resistor [tolerance=±5% power=0.25W resistance=220 package=THT]
  S1 = Pushbutton [package="[THT]"]
  S2 = Pushbutton [package="[THT]"]
  7_Segment1 = 7 Segment Display
  R6 = Resistor [tolerance=±5% power=0.25W resistance=220 package=THT]
  R7 = Resistor [tolerance=±5% power=0.25W resistance=220 package=THT]
  R8 = Resistor [tolerance=±5% power=0.25W resistance=220 package=THT]
  LED16 = LED - 5mm [color="White (8000K)" current=0.030A package="5 mm [THT]"]
  LED17 = LED - 5mm [color="White (8000K)" current=0.030A package="5 mm [THT]"]
  R9 = Resistor [tolerance=±5% power=0.25W resistance=220 package=THT]

nets:
  N1: Part1.A0, 7_Segment1.Segment_E
  N2: Part1.A1, 7_Segment1.Segment_A
  N3: Part1.A2, 7_Segment1.Segment_B
  N4: Part1.A3, 7_Segment1.Segment_D
  N5: Part1.A4/SDA, 7_Segment1.Segment_C
  N6: Part1.D8, LED6.anode, LED15.anode
  N7: Part1.D9_PWM, LED5.anode, LED14.anode
  N8: Part1.D10_PWM/SS, LED4.anode, LED13.anode
  N9: Part1.D11_PWM/MOSI, LED8.anode, LED11.anode
  N10: Part1.D12/MISO, LED9.anode, LED10.anode
  N11: Part1.D13/SCK, LED7.anode, LED12.anode
  N12: Part1.GND, R2.Pin_0, R3.Pin_0, R4.Pin_0, R5.Pin_0, S2.Pin_1, S2.Pin_2, 7_Segment1.common_cathode, R7.Pin_1, R8.Pin_1, R9.Pin_1
  N13: Part1.D2, 7_Segment1.Segment_F
  N14: Part1.D3_PWM, S1.Pin_1, S1.Pin_2, R6.Pin_0
  N15: Part1.D4, S2.Pin_3, S2.Pin_4, R7.Pin_0
  N16: Part1.D5_PWM, 7_Segment1.Segment_G
  N17: Part1.D6_PWM, LED16.anode
  N18: Part1.D7, LED17.anode
  N19: Part1.5V, S1.Pin_3, S1.Pin_4, R6.Pin_1
  N20: LED4.cathode, LED5.cathode, LED6.cathode, R2.Pin_1
  N21: LED7.cathode, R3.Pin_1, LED8.cathode, LED9.cathode
  N22: LED10.cathode, LED11.cathode, LED12.cathode, R4.Pin_1
  N23: LED13.cathode, LED14.cathode, LED15.cathode, R5.Pin_1
  N24: R8.Pin_0, LED16.cathode
  N25: LED17.cathode, R9.Pin_0
